# Fritzing sketch circuit (saved by Fritzing 0.9.2b)
breadboards: 1

parts:
  U1 = Voltage Regulator - Variable [package="TO220 [THT]"]
  M1 = DC Motor  # not connected
  M2 = DC Motor  # not connected
  Part1 = Arduino Uno (Rev3)
  VCC1 = Battery block 9V
  R1 = Resistor [tolerance=±5% resistance=50k package=THT]
  R2 = Resistor [tolerance=±5% resistance=220 package=THT]
  IC1 = H-Bridge [package=THT]  # not connected

nets:
  N1: U1.ADJ, R1.Pin_0, R2.Pin_1
  N2: U1.OUT, R1.Pin_1
  N3: U1.IN, Part1.VIN, VCC1.+
  GND: Part1.GND, VCC1.-, R2.Pin_0

// code stored in the sketch: circuit.ino
const int motorPins[3] = {4, 5, 6};

void setup(){
	for(int i=0; i<3; i++)
		pinMode(motorPins[i], OUTPUT);
	digitalWrite(motorPin[0], HIGH);
	digitalWrite(motorPin[1], LOW);
}

void loop(){
	for(int i=0; i<255; i++){
		analogWrite(motorPin[2], i);
		delay(10);
	}	
	for(int i=255; i>0; i--){
		analogWrite(motorPin[2], i);
		delay(10);
	}	
}
